// Logisim project projeto.circ as structural Verilog: 17 circuits, main circuit main
module main (
  input  [3:0] chute,
  input  confirmar,
  output acertou
);

  wire DECODER_a_2, DECODER_b_2, DECODER_c_2, DECODER_e, DECODER_f, DECODER_g, DECODER_out_8, random_out;
  wire [7:0] temperatura_p1, temperatura_p2;

  Button random (.out(random_out));
  // RGBLed #(.multibit("true")) temperatura: pin names not known; wires that end beside it: temperatura_p1, temperatura_p2
  GAME game_1 (
    .confirmar(confirmar), .\new (random_out), .chute(chute), .red(temperatura_p1), .blue(temperatura_p2),
    .out_6(acertou));
  _7seg DECODER (
    .a_2(DECODER_a_2), .b_2(DECODER_b_2), .c_2(DECODER_c_2), .out_8(DECODER_out_8), .e(DECODER_e),
    .f(DECODER_f), .g(DECODER_g), .d(chute[3]), .c(chute[2]), .b(chute[1]), .a(chute[0]));
  _7_Segment_Display u_7_segment_display_1 (
    .g(DECODER_g), .f(DECODER_f), .a(DECODER_a_2), .b(DECODER_b_2), .e(DECODER_e), .d(DECODER_out_8),
    .c(DECODER_c_2));  // open: dp

  // Other names for the same wires on the sheet: cf = confirmar
endmodule

module _7seg (
  input  d,
  input  c,
  input  b,
  input  a,
  output a_2,
  output b_2,
  output c_2,
  output out_8,
  output e,
  output f,
  output g
);

  a a_1 (.a(d), .b(c), .c(b), .d(a), .x(a_2));
  b b_1 (.a(d), .b(c), .c(b), .d(a), .x(b_2));
  c c_1 (.a(d), .b(c), .c(b), .d(a), .x(c_2));
  d d_1 (.a(d), .b(c), .c(b), .d(a), .x(out_8));
  e e_1 (.a(d), .b(c), .c(b), .d(a), .x(e));
  f f_1 (.a(d), .b(c), .c(b), .d(a), .x(f));
  g g_1 (.a(d), .b(c), .c(b), .d(a), .x(g));
  _7_Segment_Display u_7_segment_display_1 (.g(g), .f(f), .a(a_2), .b(b_2), .e(e), .d(out_8), .c(c_2));  // open: dp

  // Other names for the same wires on the sheet: A_t = a_2; B_t = b_2; C_t = c_2; D_t = out_8
endmodule

module a (
  input  a,
  input  b,
  input  c,
  input  d,
  output x
);

  wire and_1_out, and_2_out, and_3_out, and_4_out, and_5_out, and_6_out, not_1_out, not_2_out, not_3_out,
       not_4_out, not_5_out, not_6_out, not_7_out;

  not not_1 (not_1_out, b);
  and and_1 (and_1_out, not_1_out, not_2_out);
  not not_2 (not_2_out, d);
  not not_3 (not_3_out, a);
  and and_2 (and_2_out, not_3_out, c);
  not not_4 (not_4_out, a);
  and and_3 (and_3_out, not_4_out, b, d);
  and and_4 (and_4_out, b, c);
  not not_5 (not_5_out, b);
  and and_5 (and_5_out, a, not_5_out, not_6_out);
  not not_6 (not_6_out, c);
  and and_6 (and_6_out, a, not_7_out);
  not not_7 (not_7_out, d);
  or or_1 (x, and_1_out, and_2_out, and_3_out, and_4_out, and_5_out, and_6_out);
endmodule

module b (
  input  a,
  input  b,
  input  c,
  input  d,
  output x
);

  wire and_1_out, and_2_out, and_3_out, and_4_out, and_5_out, not_1_out, not_2_out, not_3_out, not_4_out,
       not_5_out, not_6_out, not_7_out, not_8_out, not_9_out;

  not not_1 (not_1_out, a);
  and and_1 (and_1_out, not_1_out, not_2_out);
  not not_2 (not_2_out, b);
  not not_3 (not_3_out, a);
  and and_2 (and_2_out, not_3_out, not_4_out, not_5_out);
  not not_4 (not_4_out, c);
  not not_5 (not_5_out, d);
  not not_6 (not_6_out, b);
  and and_3 (and_3_out, not_6_out, not_7_out);
  not not_7 (not_7_out, d);
  not not_8 (not_8_out, a);
  and and_4 (and_4_out, not_8_out, c, d);
  not not_9 (not_9_out, c);
  and and_5 (and_5_out, a, not_9_out, d);
  or or_1 (x, and_1_out, and_2_out, and_3_out, and_4_out, and_5_out);
endmodule

module c (
  input  a,
  input  b,
  input  c,
  input  d,
  output x
);

  wire and_1_out, and_2_out, and_3_out, and_4_out, and_5_out, not_1_out, not_2_out, not_3_out, not_4_out,
       not_5_out, not_6_out;

  not not_1 (not_1_out, a);
  and and_1 (and_1_out, not_1_out, not_2_out);
  not not_2 (not_2_out, c);
  not not_3 (not_3_out, a);
  and and_2 (and_2_out, not_3_out, d);
  not not_4 (not_4_out, c);
  and and_3 (and_3_out, not_4_out, d);
  not not_5 (not_5_out, a);
  and and_4 (and_4_out, not_5_out, b);
  and and_5 (and_5_out, a, not_6_out);
  not not_6 (not_6_out, b);
  or or_1 (x, and_1_out, and_2_out, and_3_out, and_4_out, and_5_out);
endmodule

module d (
  input  a,
  input  b,
  input  c,
  input  d,
  output x
);

  wire and_1_out, and_2_out, and_3_out, and_4_out, and_5_out, not_1_out, not_2_out, not_3_out, not_4_out,
       not_5_out, not_6_out, not_7_out;

  not not_1 (not_1_out, a);
  and and_1 (and_1_out, not_1_out, not_2_out, not_3_out);
  not not_2 (not_2_out, b);
  not not_3 (not_3_out, d);
  not not_4 (not_4_out, b);
  and and_2 (and_2_out, not_4_out, c, d);
  and and_3 (and_3_out, b, not_5_out, d);
  not not_5 (not_5_out, c);
  and and_4 (and_4_out, b, c, not_6_out);
  not not_6 (not_6_out, d);
  and and_5 (and_5_out, a, not_7_out);
  not not_7 (not_7_out, c);
  or or_1 (x, and_1_out, and_2_out, and_3_out, and_4_out, and_5_out);
endmodule

module e (
  input  a,
  input  b,
  input  c,
  input  d,
  output x
);

  wire and_1_out, and_2_out, and_3_out, and_4_out, not_1_out, not_2_out, not_3_out;

  not not_1 (not_1_out, b);
  and and_1 (and_1_out, not_1_out, not_2_out);
  not not_2 (not_2_out, d);
  and and_2 (and_2_out, c, not_3_out);
  not not_3 (not_3_out, d);
  and and_3 (and_3_out, a, c);
  and and_4 (and_4_out, a, b);
  or or_1 (x, and_1_out, and_2_out, and_3_out, and_4_out);
endmodule

module f (
  input  a,
  input  b,
  input  c,
  input  d,
  output x
);

  wire and_1_out, and_2_out, and_3_out, and_4_out, and_5_out, not_1_out, not_2_out, not_3_out, not_4_out,
       not_5_out, not_6_out;

  not not_1 (not_1_out, c);
  and and_1 (and_1_out, not_1_out, not_2_out);
  not not_2 (not_2_out, d);
  not not_3 (not_3_out, a);
  and and_2 (and_2_out, not_3_out, b, not_4_out);
  not not_4 (not_4_out, c);
  and and_3 (and_3_out, b, not_5_out);
  not not_5 (not_5_out, d);
  and and_4 (and_4_out, a, not_6_out);
  not not_6 (not_6_out, b);
  and and_5 (and_5_out, a, c);
  or or_1 (x, and_1_out, and_2_out, and_3_out, and_4_out, and_5_out);
endmodule

module g (
  input  a,
  input  b,
  input  c,
  input  d,
  output x
);

  wire and_1_out, and_2_out, and_3_out, and_4_out, and_5_out, not_1_out, not_2_out, not_3_out, not_4_out,
       not_5_out;

  not not_1 (not_1_out, b);
  and and_1 (and_1_out, not_1_out, c);
  and and_2 (and_2_out, c, not_2_out);
  not not_2 (not_2_out, d);
  not not_3 (not_3_out, a);
  and and_3 (and_3_out, not_3_out, b, not_4_out);
  not not_4 (not_4_out, c);
  and and_4 (and_4_out, a, not_5_out);
  not not_5 (not_5_out, b);
  and and_5 (and_5_out, a, d);
  or or_1 (x, and_1_out, and_2_out, and_3_out, and_4_out, and_5_out);
endmodule

module GAME (
  input  confirmar,
  input  \new ,
  input  [3:0] chute,
  output [7:0] red,
  output [7:0] blue,
  output out_6
);

  wire a_c, igual, zerar;
  wire [3:0] aleat, \diferença , maior, menor, not_2_out, seconf;

  not not_1 (zerar, confirmar);
  assign red[7:4] = seconf & not_2_out;  // AND_Gate and_1, 4 bits wide
  assign not_2_out = ~\diferença ;  // NOT_Gate not_2, 4 bits wide
  sinal_estendido sinal_estendido_1 (.in_1(confirmar), .out_2(seconf));
  Random #(.width(4)) random_1 (.clk(\new ), .out(aleat));  // open: next, clr
  assign blue[7:4] = \diferença  & seconf;  // AND_Gate and_2, 4 bits wide
  subtracao subtracao_1 (.in_1(aleat), .in_2(chute), .n(a_c), .igual(igual));  // open: saída
  and and_3 (out_6, confirmar, igual);
  multiplexador multiplexador_1 (.a(aleat), .b(chute), .s(a_c), .x(maior));
  multiplexador multiplexador_2 (.a(chute), .b(aleat), .s(a_c), .x(menor));
  subtracao subtracao_2 (.\saída (\diferença ), .in_1(maior), .in_2(menor));  // open: n, igual

  assign blue[3:0] = 4'b0000;
  assign red[3:0] = 4'b0000;
endmodule

module multiplexador (
  input  [3:0] a,
  input  [3:0] b,
  input  s,
  output [3:0] x
);

  wire [3:0] and_1_out, and_2_out, bit_extender_1_out, not_1_out;

  assign not_1_out = ~bit_extender_1_out;  // NOT_Gate not_1, 4 bits wide
  assign bit_extender_1_out = {{3{s}}, s};  // Bit_Extender bit_extender_1
  assign and_1_out = b & bit_extender_1_out;  // AND_Gate and_1, 4 bits wide
  assign and_2_out = a & not_1_out;  // AND_Gate and_2, 4 bits wide
  assign x = and_1_out | and_2_out;  // OR_Gate or_1, 4 bits wide
endmodule

module sinal_estendido (
  input  in_1,
  output [3:0] out_2
);


  assign out_2 = {4{in_1}};
endmodule

module subtracao (
  input  [3:0] in_1,
  input  [3:0] in_2,
  output igual,
  output [3:0] \saída ,
  output n
);

  wire caixasub_1_cout, caixasub_2_cout, caixasub_3_cout;
  wire [3:0] not_1_out;

  caixasub caixasub_1 (.A(in_1[0]), .cin(1'b0), .B(in_2[0]), .cout(caixasub_1_cout), .S(\saída [0]));
  caixasub caixasub_2 (.A(in_1[1]), .cin(caixasub_1_cout), .B(in_2[1]), .cout(caixasub_2_cout), .S(\saída [1]));
  caixasub caixasub_3 (.A(in_1[2]), .cin(caixasub_2_cout), .B(in_2[2]), .cout(caixasub_3_cout), .S(\saída [2]));
  caixasub caixasub_4 (.A(in_1[3]), .cin(caixasub_3_cout), .B(in_2[3]), .cout(n), .S(\saída [3]));
  assign not_1_out = ~\saída ;  // NOT_Gate not_1, 4 bits wide
  and and_1 (igual, not_1_out[0], not_1_out[1], not_1_out[2], not_1_out[3]);

  // Other names for the same wires on the sheet: _3a = in_1[0]; _2a = in_1[1]; _1a = in_1[2]; _0a = in_1[3];
  //   _3b = in_2[0]; _2b = in_2[1]; _1b = in_2[2]; _0b = in_2[3]
endmodule

module caixasub (
  input  A,
  input  cin,
  input  B,
  output cout,
  output S
);

  wire and_1_out, and_2_out, and_3_out, and_4_out, and_5_out, and_6_out, and_7_out, not_1_out, not_2_out,
       not_3_out, not_4_out, not_5_out, not_6_out, not_7_out, not_8_out;

  not not_1 (not_1_out, A);
  not not_2 (not_2_out, A);
  not not_3 (not_3_out, A);
  not not_4 (not_4_out, cin);
  not not_5 (not_5_out, A);
  not not_6 (not_6_out, B);
  not not_7 (not_7_out, cin);
  not not_8 (not_8_out, B);
  and and_1 (and_1_out, not_1_out, B);
  and and_2 (and_2_out, not_2_out, cin);
  and and_3 (and_3_out, cin, B);
  and and_4 (and_4_out, not_3_out, not_4_out, B);
  and and_5 (and_5_out, not_5_out, cin, not_6_out);
  and and_6 (and_6_out, A, not_7_out, not_8_out);
  and and_7 (and_7_out, A, cin, B);
  or or_1 (cout, and_1_out, and_2_out, and_3_out);
  or or_2 (S, and_4_out, and_5_out, and_6_out, and_7_out);
endmodule

module flipflopd_cor (
  input  slv,
  input  slv_2,
  input  [7:0] in_3,
  output [7:0] out_4
);

  wire gmb_1_s, gmb_2_s, gmb_3_s, gmb_4_s, gmb_5_s, gmb_6_s, gmb_7_s, gmb_8_s;

  gmb gmb_1 (.slv(slv_2), .v(in_3[0]), .zr(slv), .s(gmb_1_s));
  gmb gmb_2 (.slv(slv_2), .v(in_3[1]), .zr(slv), .s(gmb_2_s));
  gmb gmb_3 (.slv(slv_2), .v(in_3[2]), .zr(slv), .s(gmb_3_s));
  gmb gmb_4 (.slv(slv_2), .v(in_3[3]), .zr(slv), .s(gmb_4_s));
  gmb gmb_5 (.slv(slv_2), .v(in_3[4]), .zr(slv), .s(gmb_5_s));
  gmb gmb_6 (.slv(slv_2), .v(in_3[5]), .zr(slv), .s(gmb_6_s));
  gmb gmb_7 (.slv(slv_2), .v(in_3[6]), .zr(slv), .s(gmb_7_s));
  gmb gmb_8 (.slv(slv_2), .v(in_3[7]), .zr(slv), .s(gmb_8_s));
  D_Flip_Flop d_ff_1 (.clk(gmb_1_s), .D(slv_2), .Q(out_4[0]));  // open: Qn, preset, reset
  D_Flip_Flop d_ff_2 (.clk(gmb_2_s), .D(slv_2), .Q(out_4[1]));  // open: Qn, preset, reset
  D_Flip_Flop d_ff_3 (.clk(gmb_3_s), .D(slv_2), .Q(out_4[2]));  // open: Qn, preset, reset
  D_Flip_Flop d_ff_4 (.clk(gmb_4_s), .D(slv_2), .Q(out_4[3]));  // open: Qn, preset, reset
  D_Flip_Flop d_ff_5 (.clk(gmb_5_s), .D(slv_2), .Q(out_4[4]));  // open: Qn, preset, reset
  D_Flip_Flop d_ff_6 (.clk(gmb_6_s), .D(slv_2), .Q(out_4[5]));  // open: Qn, preset, reset
  D_Flip_Flop d_ff_7 (.clk(gmb_7_s), .D(slv_2), .Q(out_4[6]));  // open: Qn, preset, reset
  D_Flip_Flop d_ff_8 (.clk(gmb_8_s), .D(slv_2), .Q(out_4[7]));  // open: Qn, preset, reset

  // Other names for the same wires on the sheet: a = in_3[0]; b = in_3[1]; c = in_3[2]; d = in_3[3]; e = in_3[4];
  //   f = in_3[5]; g = in_3[6]; h = in_3[7]; at = out_4[0]; bt = out_4[1]; ct = out_4[2]; dt = out_4[3];
  //   et = out_4[4]; ft = out_4[5]; gt = out_4[6]; ht = out_4[7]; slv_t = slv_2; zrr = slv
endmodule

module guardarcor (
  input  [7:0] in_1,
  input  [7:0] in_2
);

  // D_Flip_Flop d_ff_1: pin names not known; wires that end beside it: in_1, in_2
endmodule

module gmb (
  input  slv,
  input  v,
  input  zr,
  output s
);

  wire and_1_out;

  and and_1 (and_1_out, slv, v);
  Multiplexer #(.enable("false")) multiplexer_1 (.in0(and_1_out), .in1(1'b1), .out(s), .sel(zr));
endmodule
