// Logisim project projeto2.circ as structural Verilog: 10 circuits, main circuit cronometro
module cronometro (
  input  xjgd,
  input  rst,
  input  [3:0] m1,
  input  [3:0] m0,
  input  clk,
  input  cfg,
  input  [3:0] s1,
  input  [3:0] s0,
  output [3:0] m1x,
  output [3:0] m0x,
  output [3:0] s1x,
  output [3:0] s0x,
  output fimx
);

  wire clka, clkb, m0_____clka, M0a_minus_minus, m1_____clka, M1_minus_minus, not_1_out, passar, s1_____clka,
       S1a_minus_minus;
  wire [3:0] M0U, M1U, not_2_out, or_1_out, S0U, S1U;

  and and_1 (clka, clk, ~passar);  // AND_Gate
  Counter #(.width(4), .max('h5), .trigger("falling")) counter_1 (
    .load(cfg), .D(M1U), .Q(m1x), .clk(m1_____clka), .clr(fimx), .down(1'b1));  // open: count, carry, preset
  Multiplexer #(.enable("false")) multiplexer_1 (.in0(M1_minus_minus), .in1(clka), .out(m1_____clka), .sel(cfg));
  and and_2 (clkb, clk, passar);
  Counter #(.width(4), .max('h9), .trigger("falling")) counter_2 (
    .load(cfg), .D(M0U), .Q(m0x), .carry(M1_minus_minus), .clk(m0_____clka), .clr(fimx), .down(1'b1));  // open: count, preset
  Multiplexer #(.enable("false")) multiplexer_2 (.in0(S1a_minus_minus), .in1(clka), .out(s1_____clka), .sel(cfg));
  Multiplexer #(.width(4), .enable("false")) multiplexer_3 (.in0(m1), .in1(4'b0000), .out(M1U), .sel(rst));
  Counter #(.width(4), .max('h5), .trigger("falling")) counter_3 (
    .load(cfg), .D(S1U), .Q(s1x), .carry(M0a_minus_minus), .clk(s1_____clka), .clr(fimx), .down(1'b1));  // open: count, preset
  Multiplexer #(.width(4), .enable("false")) multiplexer_4 (.in0(m0), .in1(4'b0000), .out(M0U), .sel(rst));
  not not_1 (not_1_out, xjgd);
  Multiplexer #(.enable("false")) multiplexer_5 (.in0(not_1_out), .in1(clk), .out(passar), .sel(cfg));
  Counter #(.width(4), .max('h9), .trigger("falling")) counter_4 (
    .load(cfg), .D(S0U), .Q(s0x), .carry(S1a_minus_minus), .clk(clka), .clr(fimx), .down(1'b1));  // open: count, preset
  Multiplexer #(.enable("false")) multiplexer_6 (.in0(M0a_minus_minus), .in1(clka), .out(m0_____clka), .sel(cfg));
  Multiplexer #(.width(4), .enable("false")) multiplexer_7 (.in0(s1), .in1(4'b0000), .out(S1U), .sel(rst));
  Multiplexer #(.width(4), .enable("false")) multiplexer_8 (.in0(s0), .in1(4'b0000), .out(S0U), .sel(rst));
  assign or_1_out = m1x | m0x | s1x | s0x;  // OR_Gate or_1, 4 bits wide
  assign not_2_out = ~or_1_out;  // NOT_Gate not_2, 4 bits wide
  and and_3 (fimx, not_2_out[0], not_2_out[1], not_2_out[2], not_2_out[3], ~cfg);  // AND_Gate

  // Other names for the same wires on the sheet: M0a[3:0] = m0x; M1a[3:0] = m1x; p = xjgd; reset = rst;
  //   S0a[3:0] = s0x; S1a[3:0] = s1x; zerr = fimx
endmodule

module game2_0 (
  input  confirmar,
  input  \new ,
  input  [3:0] chute_X,
  input  [3:0] chute_Y,
  output [7:0] red,
  output [7:0] blue,
  output Igual_X,
  output Igual_Y,
  output Igual_sm
);

  wire igual_X_t, igual_Y_t, sm, zerar;
  wire [3:0] aleat_X, aleat_Y, \diferença , not_2_out, seconf, smalxy, smchxy;

  not not_1 (zerar, confirmar);
  assign red[7:4] = seconf & not_2_out;  // AND_Gate and_1, 4 bits wide
  assign not_2_out = ~\diferença ;  // NOT_Gate not_2, 4 bits wide
  assign seconf = {{3{confirmar}}, confirmar};  // Bit_Extender bit_extender_1
  Random #(.width(4), .seed(21), .trigger("falling")) random_1 (.clk(\new ), .out(aleat_Y));  // open: next, clr
  Random #(.width(4), .trigger("falling")) random_2 (.clk(\new ), .out(aleat_X));  // open: next, clr
  assign blue[7:4] = \diferença  & seconf;  // AND_Gate and_2, 4 bits wide
  Adder #(.width(4)) adder_1 (.a(aleat_X), .b(aleat_Y), .out(smalxy));  // open: cin, cout
  Comparator #(.width(4)) comparator_1 (.a(aleat_X), .b(chute_X), .eq(igual_X_t));  // open: gt, lt
  Comparator #(.width(4)) comparator_2 (.a(aleat_Y), .b(chute_Y), .eq(igual_Y_t));  // open: gt, lt
  Adder #(.width(4)) adder_2 (.a(chute_X), .b(chute_Y), .out(smchxy));  // open: cin, cout
  Subtractor #(.width(4)) subtractor_1 (.a(smalxy), .b(smchxy), .out(\diferença ));  // open: bin, bout
  Comparator #(.width(4)) comparator_3 (.a(smalxy), .b(smchxy), .eq(sm));  // open: gt, lt
  and and_3 (Igual_X, confirmar, igual_X_t);
  and and_4 (Igual_Y, confirmar, igual_Y_t);
  and and_5 (Igual_sm, confirmar, sm);

  assign blue[3:0] = 4'b0000;
  assign red[3:0] = 4'b0000;

  // Other names for the same wires on the sheet: rndnew = \new 
endmodule

module main (
);

  wire A, A_jogando, A_venceu, Acerto, and_3_out, and_4_out, and_5_out, and_6_out, and_7_out, and_8_out, as,
       \Avançar , \Avançar_A , \Avançar_B , B, B_jogando, B_venceu, C_A, C_B, cfg, clk, comparator_1_eq,
       comparator_2_eq, comparator_2_gt, comparator_2_lt, comparator_3_eq, counter_7_q, empate, fim_A, fim_B,
       fim_de_jogo, inicio, jogando, Jogando_x, Jogando_y, m0a_t, m0b_t, m1a_t, m1b_t, or_1_out, or_2_out,
       or_3_out, or_6_out, Reset, s0a_t, s0b_t, s1a_t, s1b_t, Soma_Certa, X_Certo, Y_Certo;
  wire [3:0] as4, m0, M0a, M0b, m1, M1a, M1b, PA, PB, s0, S0a, S0b, s1, S1a, S1b, V_A, V_B, X_atual, Y_atual;
  wire [7:0] b_t, r;

  Clock clock_1 (.out(clk));
  cronometro cronometro_1 (
    .cfg(cfg), .xjgd(A_jogando), .s0(s0), .s1(s1), .m0(m0), .m1(m1), .rst(Reset), .clk(clk), .m1x(M1a),
    .m0x(M0a), .s1x(S1a), .s0x(S0a), .fimx(fim_A));
  cronometro cronometro_2 (
    .cfg(cfg), .xjgd(B_jogando), .s0(s0), .s1(s1), .m0(m0), .m1(m1), .rst(Reset), .clk(clk), .m1x(M1b),
    .m0x(M0b), .s1x(S1b), .s0x(S0b), .fimx(fim_B));
  assign as4 = {{3{as}}, as};  // Bit_Extender bit_extender_1
  and and_1 (fim_de_jogo, fim_A, fim_B);
  Counter #(.width(4), .max('h5), .trigger("falling")) counter_1 (
    .Q(m1), .clk(or_1_out), .clr(Reset));  // open: load, D, count, carry, preset, down
  or or_1 (or_1_out, m1a_t, m1b_t);
  Comparator #(.width(4), .mode("unsigned")) comparator_1 (.a(PB), .b(4'b1111), .eq(comparator_1_eq));  // open: gt, lt
  Comparator #(.width(4), .mode("unsigned")) comparator_2 (
    .a(PB), .b(PA), .gt(comparator_2_gt), .eq(comparator_2_eq), .lt(comparator_2_lt));
  Comparator #(.width(4), .mode("unsigned")) comparator_3 (.a(PA), .b(4'b1111), .eq(comparator_3_eq));  // open: gt, lt
  Counter #(.width(4), .max('h9), .trigger("falling")) counter_2 (
    .Q(m0), .clk(or_2_out), .clr(Reset));  // open: load, D, count, carry, preset, down
  or or_2 (or_2_out, m0a_t, m0b_t);
  Counter #(.width(4), .max('hf), .behavior("old")) counter_3 (
    .Q(V_A), .clk(A), .clr(\Avançar_A ));  // open: load, D, count, carry, preset
  Counter #(.width(4), .max('hf), .behavior("old")) counter_4 (
    .Q(V_B), .clk(B), .clr(\Avançar_B ));  // open: load, D, count, carry, preset
  and and_2 (empate, fim_de_jogo, comparator_2_eq);
  Counter #(.width(4), .max('h5)) counter_5 (
    .Q(s1), .clk(or_3_out), .clr(Reset));  // open: load, D, count, carry, preset, down
  or or_3 (or_3_out, s1a_t, s1b_t);
  or or_4 (B_venceu, comparator_1_eq, and_3_out);
  and and_3 (and_3_out, fim_de_jogo, comparator_2_gt);
  and and_4 (and_4_out, comparator_2_lt, fim_de_jogo);
  or or_5 (A_venceu, and_4_out, comparator_3_eq);
  Counter #(.width(4), .max('h9), .trigger("falling")) counter_6 (
    .Q(s0), .clk(or_6_out), .clr(Reset));  // open: load, D, count, carry, preset, down
  or or_6 (or_6_out, s0a_t, s0b_t);
  Counter #(.width(1), .max('h1)) counter_7 (
    .Q(counter_7_q), .clk(inicio), .clr(Reset));  // open: load, D, count, carry, preset, down
  not not_1 (cfg, counter_7_q);
  not not_2 (jogando, cfg);
  or or_7 (\Avançar , and_6_out, and_5_out);
  and and_5 (and_5_out, \Avançar_B , B_jogando);
  and and_6 (and_6_out, \Avançar_A , A_jogando);
  Button button (.out(A));
  Hex_Digit_Display hex_digit_display_1 (.value(PA));  // open: dp
  Hex_Digit_Display hex_digit_display_2 (.value(M1a));  // open: dp
  Hex_Digit_Display hex_digit_display_3 (.value(M0a));  // open: dp
  Button button_2 (.out(m1a_t));
  Button button_3 (.out(m0a_t));
  Hex_Digit_Display hex_digit_display_4 (.value(V_A));  // open: dp
  Button button_4 (.out(C_A));
  LED led_1 (.in(A_jogando));
  Hex_Digit_Display hex_digit_display_5 (.value(S1a));  // open: dp
  Hex_Digit_Display hex_digit_display_6 (.value(S0a));  // open: dp
  Button button_5 (.out(s1a_t));
  Button button_6 (.out(s0a_t));
  Button button_7 (.out(\Avançar_A ));
  LED led_2 (.in(X_Certo));
  core core_1 (
    .CA(C_A), .CB(C_B), .VA(V_A), .VB(V_B), .JOGANDO(jogando), .FIMA(fim_A), .FIMB(fim_B),
    .\AVANÇAR (\Avançar ), .ACERTO(Acerto), .RESET(Reset), .AJOGANDO(A_jogando), .BJOGANDO(B_jogando),
    .SOMACERTA(Soma_Certa), .XCERTO(X_Certo), .YCERTO(Y_Certo), .XATUAL(X_atual), .YATUAL(Y_atual),
    .JOGANDOX(Jogando_x), .JOGANDOY(Jogando_y), .R(r), .B(b_t));
  Counter #(.width(4), .max('hf)) counter_8 (
    .Q(PA), .clk(and_7_out), .clr(Reset));  // open: load, D, count, carry, preset, down
  and and_7 (and_7_out, Acerto, A_jogando);
  Counter #(.width(4), .max('hf)) counter_9 (
    .Q(PB), .clk(and_8_out), .clr(Reset));  // open: load, D, count, carry, preset, down
  and and_8 (and_8_out, Acerto, B_jogando);
  LED led_3 (.in(A_venceu));
  LED led_4 (.in(Soma_Certa));
  Hex_Digit_Display hex_digit_display_7 (.value(X_atual));  // open: dp
  LED led_5 (.in(Jogando_x));
  Button button_8 (.out(inicio));
  LED led_6 (.in(fim_de_jogo));
  LED led_7 (.in(empate));
  // RGBLed #(.multibit("true")) rgbled_1: pin names not known; wires that end beside it: r, b_t
  Hex_Digit_Display hex_digit_display_8 (.value(Y_atual));  // open: dp
  LED led_8 (.in(Jogando_y));
  LED led_9 (.in(cfg));
  Button button_9 (.out(Reset));
  LED led_10 (.in(B_venceu));
  LED led_11 (.in(Y_Certo));
  Hex_Digit_Display hex_digit_display_9 (.value(M1b));  // open: dp
  Hex_Digit_Display hex_digit_display_10 (.value(M0b));  // open: dp
  Button button_10 (.out(m1b_t));
  Button button_11 (.out(B));
  Hex_Digit_Display hex_digit_display_11 (.value(PB));  // open: dp
  Hex_Digit_Display hex_digit_display_12 (.value(S1b));  // open: dp
  Button button_12 (.out(m0b_t));
  Button button_13 (.out(s1b_t));
  Hex_Digit_Display hex_digit_display_13 (.value(V_B));  // open: dp
  Button button_14 (.out(C_B));
  LED led_12 (.in(B_jogando));
  Hex_Digit_Display hex_digit_display_14 (.value(S0b));  // open: dp
  Button button_15 (.out(s0b_t));
  Button button_16 (.out(\Avançar_B ));

  // Notes on the sheet:
  //   :
  //   +
  //   :
endmodule

module somadorencapsulado (
  input  [3:0] in_1,
  input  [3:0] in_2,
  output [4:0] out_3
);

  Adder #(.width(4)) adder_1 (.a(in_1), .b(in_2), .out(out_3[3:0]), .cout(out_3[4]));  // open: cin
endmodule

module GTN_X (
  input  in_1,
  input  Novo,
  input  [3:0] X,
  input  [3:0] Y,
  output [7:0] Vermelho,
  output [7:0] Azul,
  output X_certo,
  output Y_certo,
  output Soma_certa
);

  wire comp4_1_out_3, comp4_2_out_3, comp5_1_out_3;
  wire [4:0] \dif5_1_diferença , somadorencapsulado_1_out_3, somadorencapsulado_2_out_3;
  wire [7:0] bit_extender_1_out, cores_1_blue, cores_1_red, random_1_out;

  Random random_1 (.clk(Novo), .out(random_1_out));  // open: next, clr
  assign bit_extender_1_out = {{7{in_1}}, in_1};  // Bit_Extender bit_extender_1
  somadorencapsulado somadorencapsulado_1 (.in_1(Y), .in_2(X), .out_3(somadorencapsulado_1_out_3));
  somadorencapsulado somadorencapsulado_2 (
    .in_1(random_1_out[7:4]), .in_2(random_1_out[3:0]), .out_3(somadorencapsulado_2_out_3));
  and and_1 (X_certo, in_1, comp4_1_out_3);
  comp4 comp4_1 (.A(random_1_out[3:0]), .B(X), .out_3(comp4_1_out_3));
  and and_2 (Y_certo, in_1, comp4_2_out_3);
  comp4 comp4_2 (.A(random_1_out[7:4]), .B(Y), .out_3(comp4_2_out_3));
  and and_3 (Soma_certa, in_1, comp5_1_out_3);
  comp5 comp5_1 (.A(somadorencapsulado_2_out_3), .B(somadorencapsulado_1_out_3), .out_3(comp5_1_out_3));
  assign Vermelho = bit_extender_1_out & cores_1_red;  // AND_Gate and_4, 8 bits wide
  dif5 dif5_1 (.A(somadorencapsulado_2_out_3), .B(somadorencapsulado_1_out_3), .\DIFERENÇA (\dif5_1_diferença ));
  assign Azul = cores_1_blue & bit_extender_1_out;  // AND_Gate and_5, 8 bits wide
  cores cores_1 (.dif(\dif5_1_diferença ), .red(cores_1_red), .blue(cores_1_blue));
endmodule

module comp4 (
  input  [3:0] A,
  input  [3:0] B,
  output out_3
);

  wire [3:0] not_1_out, subtractor_1_out;

  Subtractor #(.width(4)) subtractor_1 (.a(A), .b(B), .out(subtractor_1_out));  // open: bin, bout
  assign not_1_out = ~subtractor_1_out;  // NOT_Gate not_1, 4 bits wide
  and and_1 (out_3, not_1_out[0], not_1_out[1], not_1_out[2], not_1_out[3]);
endmodule

module comp5 (
  input  [4:0] A,
  input  [4:0] B,
  output out_3
);

  wire [4:0] not_1_out, subtractor_1_out;

  assign not_1_out = ~subtractor_1_out;  // NOT_Gate not_1, 5 bits wide
  Subtractor #(.width(5)) subtractor_1 (.a(A), .b(B), .out(subtractor_1_out));  // open: bin, bout
  and and_1 (out_3, not_1_out[0], not_1_out[1], not_1_out[2], not_1_out[3], not_1_out[4]);
endmodule

module dif5 (
  input  [4:0] A,
  input  [4:0] B,
  output [4:0] \DIFERENÇA 
);

  wire s;
  wire [4:0] MAIOR, MENOR;

  Subtractor #(.width(5)) subtractor_1 (.a(A), .b(B), .bout(s));  // open: out, bin
  Subtractor #(.width(5)) subtractor_2 (.a(MAIOR), .b(MENOR), .out(\DIFERENÇA ));  // open: bin, bout
  Multiplexer #(.width(5), .enable("false")) multiplexer_1 (.in0(A), .in1(B), .out(MAIOR), .sel(s));
  Multiplexer #(.width(5), .enable("false")) multiplexer_2 (.in0(B), .in1(A), .out(MENOR), .sel(s));
endmodule

module cores (
  input  [4:0] dif,
  output [7:0] red,
  output [7:0] blue
);

  assign red = ~{dif, 3'b111};  // NOT_Gate not_1, 8 bits wide

  assign blue = {dif, 3'b111};
endmodule

module core (
  input  CA,
  input  CB,
  input  [3:0] VA,
  input  [3:0] VB,
  input  JOGANDO,
  input  FIMA,
  input  FIMB,
  input  \AVANÇAR ,
  input  RESET,
  output AJOGANDO,
  output BJOGANDO,
  output SOMACERTA,
  output [7:0] R,
  output [7:0] B,
  output XCERTO,
  output YCERTO,
  output [3:0] XATUAL,
  output [3:0] YATUAL,
  output JOGANDOX,
  output ACERTO,
  output JOGANDOY
);

  wire aacb, and_2_out, and_6_out, and_7_out, and_8_out, bacb, \cmç , comparator_1_eq, comparator_1_gt, CONF,
       counter_2_q, counter_3_q, JGNDA_B, or_1_out, or_2_out, or_3_out, zrr;
  wire [1:0] counter_1_q;
  wire [3:0] X_Y_A, X_Y_B, XG, XG_A, XG_B, YG, YG_A, YG_B;

  Register #(.width(4), .Select("low")) register_1 (.D(VA), .Q(X_Y_A), .clk(CA), .clr(RESET));  // open: en
  Register #(.width(4), .Select("low")) register_2 (.D(VB), .Q(X_Y_B), .clk(CB), .clr(RESET));  // open: en
  Button button_1 ();  // open: out
  Counter #(.width(2), .max('h2)) counter_1 (
    .Q(counter_1_q), .carry(CONF), .clk(\AVANÇAR ), .clr(or_1_out));  // open: load, D, count, preset, down
  or or_1 (or_1_out, aacb, zrr, RESET, bacb);
  and and_1 (aacb, AJOGANDO, FIMA);
  and and_2 (and_2_out, JOGANDO, zrr);
  Counter #(.width(1), .max('h1)) counter_2 (
    .Q(counter_2_q), .clk(ACERTO), .clr(and_2_out));  // open: load, D, count, carry, preset, down
  and and_3 (bacb, FIMB, BJOGANDO);
  Demultiplexer #(.width(4), .enable("false")) demultiplexer_1 (.out0(XG_A), .out1(YG_A), .in(X_Y_A), .sel(JOGANDOY));
  GTN_X gtn_x_1 (
    .Vermelho(R), .in_1(CONF), .Novo(and_2_out), .X(XATUAL), .Y(YATUAL), .Azul(B), .X_certo(XCERTO),
    .Y_certo(YCERTO), .Soma_certa(SOMACERTA));
  and and_4 (ACERTO, XCERTO, YCERTO);
  and and_5 (zrr, \cmç , counter_2_q);
  Comparator #(.width(2), .mode("unsigned")) comparator_1 (
    .a(counter_1_q), .b(2'b01), .gt(comparator_1_gt), .eq(comparator_1_eq), .lt(\cmç ));
  Counter #(.width(1), .max('h1), .trigger("falling"), .behavior("old")) counter_3 (
    .Q(counter_3_q), .clk(CONF), .clr(comparator_1_eq));  // open: load, D, count, carry, preset
  Demultiplexer #(.width(4), .enable("false")) demultiplexer_2 (.out0(XG_B), .out1(YG_B), .in(X_Y_B), .sel(JOGANDOY));
  Demultiplexer #(.enable("false")) demultiplexer_3 (.out0(AJOGANDO), .out1(BJOGANDO), .in(JOGANDO), .sel(JGNDA_B));
  Counter #(.width(1), .max('h1)) counter_4 (
    .Q(JGNDA_B), .clk(and_6_out), .clr(RESET));  // open: load, D, count, carry, preset, down
  or or_2 (or_2_out, counter_3_q, FIMA);
  and and_6 (and_6_out, or_2_out, ~FIMB);  // AND_Gate
  not not_1 (JOGANDOX, JOGANDOY);
  Multiplexer #(.width(4), .enable("false")) multiplexer_1 (.in0(XG_A), .in1(XG_B), .out(XG), .sel(BJOGANDO));
  Multiplexer #(.width(4), .enable("false")) multiplexer_2 (.in0(YG_A), .in1(YG_B), .out(YG), .sel(BJOGANDO));
  Register #(.width(4), .Select("low")) register_3 (.D(XG), .Q(XATUAL), .clk(and_7_out), .clr(or_3_out));  // open: en
  and and_7 (and_7_out, \AVANÇAR , ~JOGANDOY);  // AND_Gate
  Register #(.width(4), .Select("low")) register_4 (.D(YG), .Q(YATUAL), .clk(and_8_out), .clr(or_3_out));  // open: en
  and and_8 (and_8_out, JOGANDOY, \AVANÇAR );
  or or_3 (or_3_out, aacb, zrr, RESET, bacb);
  or or_4 (JOGANDOY, comparator_1_gt, comparator_1_eq);

  // Other names for the same wires on the sheet: AJGND = AJOGANDO; BJGND = BJOGANDO; C_A = CA; C_B = CB; FIM_A = FIMA;
  //   FIM_B = FIMB; JGND = JOGANDO; RST = RESET; S = JOGANDOY; V_A[3:0] = VA; V_B[3:0] = VB; X[3:0] = XATUAL;
  //   Y[3:0] = YATUAL

  // Notes on the sheet:
  //   ajeitar o jogando x quando trocar de jogador!!!!!!!!!!!
endmodule
